// Logisim project Tetris.circ as structural Verilog: 14 circuits, main circuit main
module ledmatrix (
);

  wire [7:0] undriven, undriven_2;

  LED LED_70 (.in(undriven[7]));
  LED LED_70_2 (.in(undriven_2[7]));
  LED LED_50 (.in(undriven[5]));
  LED LED_40 (.in(undriven[4]));
  LED LED_60 (.in(undriven[6]));
  LED LED_40_2 (.in(undriven_2[4]));
  LED LED_50_2 (.in(undriven_2[5]));
  LED LED_60_2 (.in(undriven_2[6]));
  LED LED_10 (.in(undriven[1]));
  LED LED_30 (.in(undriven[3]));
  LED LED_20 (.in(undriven[2]));
  LED LED_20_2 (.in(undriven_2[2]));
  LED LED_30_2 (.in(undriven_2[3]));
  LED LED_10_2 (.in(undriven_2[1]));
  LED LED_00 (.in(undriven[0]));
  LED LED_00_2 (.in(undriven_2[0]));
endmodule

module DisplayMemory (
  input  Reset,
  input  Write_enable,
  input  [7:0] Data_in,
  input  Clock,
  input  [7:0] Data_in_2,
  input  [7:0] Data_in_3,
  input  [7:0] Data_in_4,
  input  [7:0] Data_in_5,
  input  [7:0] Data_in_6,
  input  [7:0] Data_in_7,
  input  [7:0] Data_in_8,
  input  [7:0] Data_in_9,
  input  [7:0] Data_in_10,
  input  [7:0] Data_in_11,
  input  [7:0] Data_in_12,
  output [7:0] Data_out,
  output [7:0] Data_out_2,
  output [7:0] Data_out_3,
  output [7:0] Data_out_4,
  output [7:0] Data_out_5,
  output [7:0] Data_out_6,
  output [7:0] Data_out_7,
  output [7:0] Data_out_8,
  output [7:0] Data_out_9,
  output [7:0] Data_out_10,
  output [7:0] Data_out_11,
  output [7:0] Data_out_12
);

  wire [7:0] or_1_out, or_2_out, or_3_out, or_4_out, or_5_out, or_6_out, or_7_out, or_8_out, or_9_out,
       or_10_out, or_11_out, or_12_out;

  Register register_1 (.D(or_1_out), .en(Write_enable), .clk(Clock), .Q(Data_out), .clr(Reset));
  assign or_1_out = Data_out | Data_in;  // OR_Gate or_1, 8 bits wide
  Register register_2 (.D(or_2_out), .en(Write_enable), .clk(Clock), .Q(Data_out_2), .clr(Reset));
  assign or_2_out = Data_out_2 | Data_in_2;  // OR_Gate or_2, 8 bits wide
  Register register_3 (.D(or_3_out), .en(Write_enable), .clk(Clock), .Q(Data_out_3), .clr(Reset));
  assign or_3_out = Data_out_3 | Data_in_3;  // OR_Gate or_3, 8 bits wide
  Register register_4 (.D(or_4_out), .en(Write_enable), .clk(Clock), .Q(Data_out_4), .clr(Reset));
  assign or_4_out = Data_out_4 | Data_in_4;  // OR_Gate or_4, 8 bits wide
  Register register_5 (.D(or_5_out), .en(Write_enable), .clk(Clock), .Q(Data_out_5), .clr(Reset));
  assign or_5_out = Data_out_5 | Data_in_5;  // OR_Gate or_5, 8 bits wide
  Register register_6 (.D(or_6_out), .en(Write_enable), .clk(Clock), .Q(Data_out_6), .clr(Reset));
  assign or_6_out = Data_out_6 | Data_in_6;  // OR_Gate or_6, 8 bits wide
  Register register_7 (.D(or_7_out), .en(Write_enable), .clk(Clock), .Q(Data_out_7), .clr(Reset));
  assign or_7_out = Data_out_7 | Data_in_7;  // OR_Gate or_7, 8 bits wide
  Register register_8 (.D(or_8_out), .en(Write_enable), .clk(Clock), .Q(Data_out_8), .clr(Reset));
  assign or_8_out = Data_out_8 | Data_in_8;  // OR_Gate or_8, 8 bits wide
  Register register_9 (.D(or_9_out), .en(Write_enable), .clk(Clock), .Q(Data_out_9), .clr(Reset));
  assign or_9_out = Data_out_9 | Data_in_9;  // OR_Gate or_9, 8 bits wide
  Register register_10 (.D(or_10_out), .en(Write_enable), .clk(Clock), .Q(Data_out_10), .clr(Reset));
  assign or_10_out = Data_out_10 | Data_in_10;  // OR_Gate or_10, 8 bits wide
  Register register_11 (.D(or_11_out), .en(Write_enable), .clk(Clock), .Q(Data_out_11), .clr(Reset));
  assign or_11_out = Data_out_11 | Data_in_11;  // OR_Gate or_11, 8 bits wide
  Register register_12 (.D(or_12_out), .en(Write_enable), .clk(Clock), .Q(Data_out_12), .clr(Reset));
  assign or_12_out = Data_out_12 | Data_in_12;  // OR_Gate or_12, 8 bits wide
endmodule

module DisplayDriver (
  input  [7:0] in_1,
  input  [3:0] in_2,
  input  [3:0] in_3,
  input  line_shift,
  input  Clock,
  input  in_6,
  input  Reset,
  output [7:0] out_8,
  output [7:0] out_9,
  output [7:0] out_10,
  output [7:0] out_11,
  output [7:0] out_12,
  output [7:0] out_13,
  output [7:0] out_14,
  output [7:0] out_15,
  output [7:0] out_16,
  output [7:0] out_17,
  output [7:0] out_18,
  output [7:0] out_19,
  output [7:0] read_line_data
);

  wire [7:0] blockmemorydriver_1_out_17, blockmemorydriver_1_out_18, blockmemorydriver_1_out_19,
       blockmemorydriver_1_out_20, blockmemorydriver_1_out_21, blockmemorydriver_1_out_22,
       blockmemorydriver_1_out_23, blockmemorydriver_1_out_24, blockmemorydriver_1_out_25,
       blockmemorydriver_1_out_26, blockmemorydriver_1_out_27, blockmemorydriver_1_out_28, dmx12x8_1_out_3,
       dmx12x8_1_out_4, dmx12x8_1_out_5, dmx12x8_1_out_6, dmx12x8_1_out_7, dmx12x8_1_out_8, dmx12x8_1_out_9,
       dmx12x8_1_out_10, dmx12x8_1_out_11, dmx12x8_1_out_12, dmx12x8_1_out_13, dmx12x8_1_out_14,
       dmx12x8_2_out_3, dmx12x8_2_out_4, dmx12x8_2_out_5, dmx12x8_2_out_6, dmx12x8_2_out_7, dmx12x8_2_out_8,
       dmx12x8_2_out_9, dmx12x8_2_out_10, dmx12x8_2_out_11, dmx12x8_2_out_12, dmx12x8_2_out_13,
       dmx12x8_2_out_14;

  DMX12x8 dmx12x8_1 (
    .in_1(in_1), .in_2(in_2), .out_3(dmx12x8_1_out_3), .out_4(dmx12x8_1_out_4), .out_5(dmx12x8_1_out_5),
    .out_6(dmx12x8_1_out_6), .out_7(dmx12x8_1_out_7), .out_8(dmx12x8_1_out_8), .out_9(dmx12x8_1_out_9),
    .out_10(dmx12x8_1_out_10), .out_11(dmx12x8_1_out_11), .out_12(dmx12x8_1_out_12),
    .out_13(dmx12x8_1_out_13), .out_14(dmx12x8_1_out_14));
  BlockMemoryDriver blockmemorydriver_1 (
    .line_shift(line_shift), .write_enable(in_6), .Reset(Reset), .in_1(dmx12x8_1_out_3),
    .in_2(dmx12x8_1_out_4), .in_3(dmx12x8_1_out_5), .in_4(dmx12x8_1_out_6), .in_5(dmx12x8_1_out_7),
    .in_6(dmx12x8_1_out_8), .in_7(dmx12x8_1_out_9), .in_8(dmx12x8_1_out_10), .in_9(dmx12x8_1_out_11),
    .in_10(dmx12x8_1_out_12), .in_11(dmx12x8_1_out_13), .in_12(dmx12x8_1_out_14),
    .out_17(blockmemorydriver_1_out_17), .out_18(blockmemorydriver_1_out_18),
    .out_19(blockmemorydriver_1_out_19), .out_20(blockmemorydriver_1_out_20),
    .out_21(blockmemorydriver_1_out_21), .out_22(blockmemorydriver_1_out_22),
    .out_23(blockmemorydriver_1_out_23), .out_24(blockmemorydriver_1_out_24),
    .out_25(blockmemorydriver_1_out_25), .out_26(blockmemorydriver_1_out_26),
    .out_27(blockmemorydriver_1_out_27), .out_28(blockmemorydriver_1_out_28), .Clock(Clock));
  DMX12x8 dmx12x8_2 (
    .in_1(in_1), .in_2(in_2), .out_3(dmx12x8_2_out_3), .out_4(dmx12x8_2_out_4), .out_5(dmx12x8_2_out_5),
    .out_6(dmx12x8_2_out_6), .out_7(dmx12x8_2_out_7), .out_8(dmx12x8_2_out_8), .out_9(dmx12x8_2_out_9),
    .out_10(dmx12x8_2_out_10), .out_11(dmx12x8_2_out_11), .out_12(dmx12x8_2_out_12),
    .out_13(dmx12x8_2_out_13), .out_14(dmx12x8_2_out_14));
  OR12 or12_1 (
    .in_13(blockmemorydriver_1_out_17), .in_14(blockmemorydriver_1_out_18),
    .in_15(blockmemorydriver_1_out_19), .in_16(blockmemorydriver_1_out_20),
    .in_17(blockmemorydriver_1_out_21), .in_18(blockmemorydriver_1_out_22),
    .in_19(blockmemorydriver_1_out_23), .in_20(blockmemorydriver_1_out_24),
    .in_21(blockmemorydriver_1_out_25), .in_22(blockmemorydriver_1_out_26),
    .in_23(blockmemorydriver_1_out_27), .in_24(blockmemorydriver_1_out_28), .in_1(dmx12x8_2_out_3),
    .in_2(dmx12x8_2_out_4), .in_3(dmx12x8_2_out_5), .in_4(dmx12x8_2_out_6), .in_5(dmx12x8_2_out_7),
    .in_6(dmx12x8_2_out_8), .in_7(dmx12x8_2_out_9), .in_8(dmx12x8_2_out_10), .in_9(dmx12x8_2_out_11),
    .in_10(dmx12x8_2_out_12), .in_11(dmx12x8_2_out_13), .in_12(dmx12x8_2_out_14), .out_25(out_8),
    .out_26(out_9), .out_27(out_10), .out_28(out_11), .out_29(out_12), .out_30(out_13), .out_31(out_14),
    .out_32(out_15), .out_33(out_16), .out_34(out_17), .out_35(out_18), .out_36(out_19));
  MUX12x8 mux12x8_1 (
    .in_1(out_8), .in_2(out_9), .in_3(out_10), .in_4(out_11), .in_5(out_12), .in_6(out_13), .in_7(out_14),
    .in_8(out_15), .in_9(out_16), .in_10(out_17), .in_11(out_18), .in_12(out_19), .in_13(in_3),
    .out_14(read_line_data));

  // Notes on the sheet:
  //   write line data
  //   write line number
  //   read line number
  //   write enable
  //   Display output
endmodule

module BlockMemory (
  input  WE,
  input  CLK,
  input  Reset,
  input  [7:0] in_4,
  input  [7:0] in_5,
  input  [7:0] in_6,
  input  [7:0] in_7,
  input  [7:0] in_8,
  input  [7:0] in_9,
  input  [7:0] in_10,
  input  [7:0] in_11,
  input  [7:0] in_12,
  input  [7:0] in_13,
  input  [7:0] in_14,
  input  [7:0] in_15,
  output [7:0] out_16,
  output [7:0] out_17,
  output [7:0] out_18,
  output [7:0] out_19,
  output [7:0] out_20,
  output [7:0] out_21,
  output [7:0] out_22,
  output [7:0] out_23,
  output [7:0] out_24,
  output [7:0] out_25,
  output [7:0] out_26,
  output [7:0] out_27
);

  Register register_1 (.D(in_4), .en(WE), .clk(CLK), .Q(out_16), .clr(Reset));
  Register register_2 (.D(in_5), .en(WE), .clk(CLK), .Q(out_17), .clr(Reset));
  Register register_3 (.D(in_6), .en(WE), .clk(CLK), .Q(out_18), .clr(Reset));
  Register register_4 (.D(in_7), .en(WE), .clk(CLK), .Q(out_19), .clr(Reset));
  Register register_5 (.D(in_8), .en(WE), .clk(CLK), .Q(out_20), .clr(Reset));
  Register register_6 (.D(in_9), .en(WE), .clk(CLK), .Q(out_21), .clr(Reset));
  Register register_7 (.D(in_10), .en(WE), .clk(CLK), .Q(out_22), .clr(Reset));
  Register register_8 (.D(in_11), .en(WE), .clk(CLK), .Q(out_23), .clr(Reset));
  Register register_9 (.D(in_12), .en(WE), .clk(CLK), .Q(out_24), .clr(Reset));
  Register register_10 (.D(in_13), .en(WE), .clk(CLK), .Q(out_25), .clr(Reset));
  Register register_11 (.D(in_14), .en(WE), .clk(CLK), .Q(out_26), .clr(Reset));
  Register register_12 (.D(in_15), .en(WE), .clk(CLK), .Q(out_27), .clr(Reset));
endmodule

module BlockMemoryDriver (
  input  [7:0] in_1,
  input  [7:0] in_2,
  input  [7:0] in_3,
  input  [7:0] in_4,
  input  [7:0] in_5,
  input  [7:0] in_6,
  input  [7:0] in_7,
  input  [7:0] in_8,
  input  [7:0] in_9,
  input  [7:0] in_10,
  input  [7:0] in_11,
  input  [7:0] in_12,
  input  line_shift,
  input  write_enable,
  input  Reset,
  input  Clock,
  output [7:0] out_17,
  output [7:0] out_18,
  output [7:0] out_19,
  output [7:0] out_20,
  output [7:0] out_21,
  output [7:0] out_22,
  output [7:0] out_23,
  output [7:0] out_24,
  output [7:0] out_25,
  output [7:0] out_26,
  output [7:0] out_27,
  output [7:0] out_28
);

  wire or_1_out;
  wire [7:0] mask12x8_1_out_14, mask12x8_1_out_15, mask12x8_1_out_16, mask12x8_1_out_17, mask12x8_1_out_18,
       mask12x8_1_out_19, mask12x8_1_out_20, mask12x8_1_out_21, mask12x8_1_out_22, mask12x8_1_out_23,
       mask12x8_1_out_24, mask12x8_1_out_25, mask12x8_2_out_14, mask12x8_2_out_15, mask12x8_2_out_16,
       mask12x8_2_out_17, mask12x8_2_out_18, mask12x8_2_out_19, mask12x8_2_out_20, mask12x8_2_out_21,
       mask12x8_2_out_22, mask12x8_2_out_23, mask12x8_2_out_24, or12_1_out_25, or12_1_out_26, or12_1_out_27,
       or12_1_out_28, or12_1_out_29, or12_1_out_30, or12_1_out_31, or12_1_out_32, or12_1_out_33,
       or12_1_out_34, or12_1_out_35, or12_1_out_36, or12_2_out_25, or12_2_out_26, or12_2_out_27,
       or12_2_out_28, or12_2_out_29, or12_2_out_30, or12_2_out_31, or12_2_out_32, or12_2_out_33,
       or12_2_out_34, or12_2_out_35, or12_2_out_36;
  wire [11:0] not_1_out;

  OR12 or12_1 (
    .in_13(in_1), .in_14(in_2), .in_15(in_3), .in_16(in_4), .in_17(in_5), .in_18(in_6), .in_19(in_7),
    .in_20(in_8), .in_21(in_9), .in_22(in_10), .in_23(in_11), .in_24(in_12), .in_1(out_17), .in_2(out_18),
    .in_3(out_19), .in_4(out_20), .in_5(out_21), .in_6(out_22), .in_7(out_23), .in_8(out_24), .in_9(out_25),
    .in_10(out_26), .in_11(out_27), .in_12(out_28), .out_25(or12_1_out_25), .out_26(or12_1_out_26),
    .out_27(or12_1_out_27), .out_28(or12_1_out_28), .out_29(or12_1_out_29), .out_30(or12_1_out_30),
    .out_31(or12_1_out_31), .out_32(or12_1_out_32), .out_33(or12_1_out_33), .out_34(or12_1_out_34),
    .out_35(or12_1_out_35), .out_36(or12_1_out_36));
  or or_1 (or_1_out, line_shift, write_enable);
  Mask12x8 mask12x8_1 (
    .in_1(or12_1_out_25), .in_2(or12_1_out_26), .in_3(or12_1_out_27), .in_4(or12_1_out_28),
    .in_5(or12_1_out_29), .in_6(or12_1_out_30), .in_7(or12_1_out_31), .in_8(or12_1_out_32),
    .in_9(or12_1_out_33), .in_10(or12_1_out_34), .in_11(or12_1_out_35), .in_12(or12_1_out_36),
    .in_13(not_1_out), .out_14(mask12x8_1_out_14), .out_15(mask12x8_1_out_15), .out_16(mask12x8_1_out_16),
    .out_17(mask12x8_1_out_17), .out_18(mask12x8_1_out_18), .out_19(mask12x8_1_out_19),
    .out_20(mask12x8_1_out_20), .out_21(mask12x8_1_out_21), .out_22(mask12x8_1_out_22),
    .out_23(mask12x8_1_out_23), .out_24(mask12x8_1_out_24), .out_25(mask12x8_1_out_25));
  assign not_1_out = ~{12{line_shift}};  // NOT_Gate not_1, 12 bits wide
  Mask12x8 mask12x8_2 (
    .in_1(out_17), .in_2(out_18), .in_3(out_19), .in_4(out_20), .in_5(out_21), .in_6(out_22), .in_7(out_23),
    .in_8(out_24), .in_9(out_25), .in_10(out_26), .in_11(out_27), .in_12(out_28), .in_13({12{line_shift}}),
    .out_14(mask12x8_2_out_14), .out_15(mask12x8_2_out_15), .out_16(mask12x8_2_out_16),
    .out_17(mask12x8_2_out_17), .out_18(mask12x8_2_out_18), .out_19(mask12x8_2_out_19),
    .out_20(mask12x8_2_out_20), .out_21(mask12x8_2_out_21), .out_22(mask12x8_2_out_22),
    .out_23(mask12x8_2_out_23), .out_24(mask12x8_2_out_24));  // open: out_25
  OR12 or12_2 (
    .in_13(mask12x8_1_out_14), .in_14(mask12x8_1_out_15), .in_15(mask12x8_1_out_16),
    .in_16(mask12x8_1_out_17), .in_17(mask12x8_1_out_18), .in_18(mask12x8_1_out_19),
    .in_19(mask12x8_1_out_20), .in_20(mask12x8_1_out_21), .in_21(mask12x8_1_out_22),
    .in_22(mask12x8_1_out_23), .in_23(mask12x8_1_out_24), .in_24(mask12x8_1_out_25), .in_1({8{1'b0}}),
    .in_2(mask12x8_2_out_14), .in_3(mask12x8_2_out_15), .in_4(mask12x8_2_out_16), .in_5(mask12x8_2_out_17),
    .in_6(mask12x8_2_out_18), .in_7(mask12x8_2_out_19), .in_8(mask12x8_2_out_20), .in_9(mask12x8_2_out_21),
    .in_10(mask12x8_2_out_22), .in_11(mask12x8_2_out_23), .in_12(mask12x8_2_out_24), .out_25(or12_2_out_25),
    .out_26(or12_2_out_26), .out_27(or12_2_out_27), .out_28(or12_2_out_28), .out_29(or12_2_out_29),
    .out_30(or12_2_out_30), .out_31(or12_2_out_31), .out_32(or12_2_out_32), .out_33(or12_2_out_33),
    .out_34(or12_2_out_34), .out_35(or12_2_out_35), .out_36(or12_2_out_36));
  BlockMemory blockmemory_1 (
    .WE(or_1_out), .CLK(Clock), .Reset(Reset), .in_4(or12_2_out_25), .in_5(or12_2_out_26),
    .in_6(or12_2_out_27), .in_7(or12_2_out_28), .in_8(or12_2_out_29), .in_9(or12_2_out_30),
    .in_10(or12_2_out_31), .in_11(or12_2_out_32), .in_12(or12_2_out_33), .in_13(or12_2_out_34),
    .in_14(or12_2_out_35), .in_15(or12_2_out_36), .out_16(out_17), .out_17(out_18), .out_18(out_19),
    .out_19(out_20), .out_20(out_21), .out_21(out_22), .out_22(out_23), .out_23(out_24), .out_24(out_25),
    .out_25(out_26), .out_26(out_27), .out_27(out_28));
endmodule

module Comp12bit (
  input  [11:0] in_1,
  input  [11:0] in_2,
  output out_3
);

  wire [11:0] xor_1_out;

  assign xor_1_out = in_1 ^ in_2;  // XOR_Gate xor_1, 12 bits wide
  nor nor_1 (out_3, xor_1_out[0], xor_1_out[1], xor_1_out[2], xor_1_out[3], xor_1_out[4], xor_1_out[5], xor_1_out[6], xor_1_out[7], xor_1_out[8], xor_1_out[9], xor_1_out[10], xor_1_out[11]);
endmodule

module GTEQ12 (
  input  [3:0] in_1,
  output o0,
  output o1,
  output o2,
  output o3,
  output o4,
  output o5,
  output o6,
  output o7,
  output o8,
  output o9,
  output o10,
  output o11
);

  wire and_1_out, and_2_out, and_3_out, and_4_out, and_5_out, and_6_out, and_7_out, and_8_out, and_9_out,
       and_10_out, and_11_out, and_12_out;

  or or_1 (o1, in_1[0], in_1[1], in_1[2], in_1[3]);
  or or_2 (o2, in_1[1], in_1[2], in_1[3]);
  and and_1 (and_1_out, in_1[1], in_1[0]);
  or or_3 (o3, and_1_out, in_1[2], in_1[3]);
  or or_4 (o4, in_1[2], in_1[3]);
  and and_2 (and_2_out, in_1[2], in_1[0]);
  and and_3 (and_3_out, in_1[2], in_1[1]);
  or or_5 (o5, and_2_out, and_3_out, in_1[3]);
  and and_4 (and_4_out, in_1[2], in_1[1]);
  or or_6 (o6, and_4_out, in_1[3]);
  and and_5 (and_5_out, in_1[2], in_1[1], in_1[0]);
  or or_7 (o7, and_5_out, in_1[3]);
  and and_6 (and_6_out, in_1[3], in_1[0]);
  or or_8 (o9, and_6_out, and_7_out, and_8_out);
  and and_7 (and_7_out, in_1[3], in_1[1]);
  and and_8 (and_8_out, in_1[3], in_1[2]);
  and and_9 (and_9_out, in_1[3], in_1[1]);
  or or_9 (o10, and_9_out, and_10_out);
  and and_10 (and_10_out, in_1[3], in_1[2]);
  and and_11 (and_11_out, in_1[3], in_1[1], in_1[0]);
  or or_10 (o11, and_11_out, and_12_out);
  and and_12 (and_12_out, in_1[3], in_1[2]);

  assign o0 = 1'b1;
  assign o8 = in_1[3];
endmodule

module mux12helper (
  input  [3:0] in_1,
  output o0,
  output o1,
  output o2,
  output o3,
  output o4,
  output o5,
  output o6,
  output o7,
  output o8,
  output o9,
  output o10,
  output o11
);

  wire not_1_out, not_2_out, not_3_out, not_4_out, not_5_out, not_6_out, not_7_out, not_8_out, not_9_out,
       not_10_out, not_11_out, not_12_out, not_13_out, not_14_out, not_15_out, not_16_out, not_17_out,
       not_18_out, not_19_out, not_20_out, not_21_out, not_22_out, not_23_out, not_24_out, not_25_out,
       not_26_out, not_27_out, not_28_out;

  not not_1 (not_1_out, in_1[3]);
  not not_2 (not_2_out, in_1[2]);
  not not_3 (not_3_out, in_1[1]);
  not not_4 (not_4_out, in_1[0]);
  not not_5 (not_5_out, in_1[3]);
  not not_6 (not_6_out, in_1[2]);
  not not_7 (not_7_out, in_1[1]);
  not not_8 (not_8_out, in_1[3]);
  not not_9 (not_9_out, in_1[2]);
  not not_10 (not_10_out, in_1[0]);
  not not_11 (not_11_out, in_1[3]);
  not not_12 (not_12_out, in_1[2]);
  not not_13 (not_13_out, in_1[3]);
  not not_14 (not_14_out, in_1[1]);
  not not_15 (not_15_out, in_1[0]);
  not not_16 (not_16_out, in_1[3]);
  not not_17 (not_17_out, in_1[1]);
  not not_18 (not_18_out, in_1[3]);
  not not_19 (not_19_out, in_1[0]);
  not not_20 (not_20_out, in_1[3]);
  not not_21 (not_21_out, in_1[2]);
  not not_22 (not_22_out, in_1[1]);
  not not_23 (not_23_out, in_1[0]);
  not not_24 (not_24_out, in_1[2]);
  not not_25 (not_25_out, in_1[1]);
  not not_26 (not_26_out, in_1[2]);
  not not_27 (not_27_out, in_1[0]);
  not not_28 (not_28_out, in_1[2]);
  and and_1 (o0, not_1_out, not_2_out, not_3_out, not_4_out);
  and and_2 (o1, not_5_out, not_6_out, not_7_out, in_1[0]);
  and and_3 (o2, not_8_out, not_9_out, in_1[1], not_10_out);
  and and_4 (o3, not_11_out, not_12_out, in_1[1], in_1[0]);
  and and_5 (o4, not_13_out, in_1[2], not_14_out, not_15_out);
  and and_6 (o5, not_16_out, in_1[2], not_17_out, in_1[0]);
  and and_7 (o6, not_18_out, in_1[2], in_1[1], not_19_out);
  and and_8 (o7, not_20_out, in_1[2], in_1[1], in_1[0]);
  and and_9 (o8, in_1[3], not_21_out, not_22_out, not_23_out);
  and and_10 (o9, in_1[3], not_24_out, not_25_out, in_1[0]);
  and and_11 (o10, in_1[3], not_26_out, in_1[1], not_27_out);
  and and_12 (o11, in_1[3], not_28_out, in_1[1], in_1[0]);
endmodule

module MUX12x8 (
  input  [7:0] in_1,
  input  [7:0] in_2,
  input  [7:0] in_3,
  input  [7:0] in_4,
  input  [7:0] in_5,
  input  [7:0] in_6,
  input  [7:0] in_7,
  input  [7:0] in_8,
  input  [7:0] in_9,
  input  [7:0] in_10,
  input  [7:0] in_11,
  input  [7:0] in_12,
  input  [3:0] in_13,
  output [7:0] out_14
);

  wire mux12helper_1_o0, mux12helper_1_o1, mux12helper_1_o2, mux12helper_1_o3, mux12helper_1_o4,
       mux12helper_1_o5, mux12helper_1_o6, mux12helper_1_o7, mux12helper_1_o8, mux12helper_1_o9,
       mux12helper_1_o10, mux12helper_1_o11;
  wire [7:0] mask8bit_1_out_3, mask8bit_2_out_3, mask8bit_3_out_3, mask8bit_4_out_3, mask8bit_5_out_3,
       mask8bit_6_out_3, mask8bit_7_out_3, mask8bit_8_out_3, mask8bit_9_out_3, mask8bit_10_out_3,
       mask8bit_11_out_3, mask8bit_12_out_3;

  Mask8bit mask8bit_1 (.in_1(in_1), .in_2(mux12helper_1_o0), .out_3(mask8bit_1_out_3));
  mux12helper mux12helper_1 (
    .in_1(in_13), .o0(mux12helper_1_o0), .o1(mux12helper_1_o1), .o2(mux12helper_1_o2), .o3(mux12helper_1_o3),
    .o4(mux12helper_1_o4), .o5(mux12helper_1_o5), .o6(mux12helper_1_o6), .o7(mux12helper_1_o7),
    .o8(mux12helper_1_o8), .o9(mux12helper_1_o9), .o10(mux12helper_1_o10), .o11(mux12helper_1_o11));
  Mask8bit mask8bit_2 (.in_1(in_2), .in_2(mux12helper_1_o1), .out_3(mask8bit_2_out_3));
  Mask8bit mask8bit_3 (.in_1(in_3), .in_2(mux12helper_1_o2), .out_3(mask8bit_3_out_3));
  Mask8bit mask8bit_4 (.in_1(in_4), .in_2(mux12helper_1_o3), .out_3(mask8bit_4_out_3));
  Mask8bit mask8bit_5 (.in_1(in_5), .in_2(mux12helper_1_o4), .out_3(mask8bit_5_out_3));
  Mask8bit mask8bit_6 (.in_1(in_6), .in_2(mux12helper_1_o5), .out_3(mask8bit_6_out_3));
  Mask8bit mask8bit_7 (.in_1(in_7), .in_2(mux12helper_1_o6), .out_3(mask8bit_7_out_3));
  Mask8bit mask8bit_8 (.in_1(in_8), .in_2(mux12helper_1_o7), .out_3(mask8bit_8_out_3));
  Mask8bit mask8bit_9 (.in_1(in_9), .in_2(mux12helper_1_o8), .out_3(mask8bit_9_out_3));
  Mask8bit mask8bit_10 (.in_1(in_10), .in_2(mux12helper_1_o9), .out_3(mask8bit_10_out_3));
  Mask8bit mask8bit_11 (.in_1(in_11), .in_2(mux12helper_1_o10), .out_3(mask8bit_11_out_3));
  Mask8bit mask8bit_12 (.in_1(in_12), .in_2(mux12helper_1_o11), .out_3(mask8bit_12_out_3));
  assign out_14 = mask8bit_1_out_3 | mask8bit_2_out_3 | mask8bit_3_out_3 | mask8bit_4_out_3 | mask8bit_5_out_3 | mask8bit_6_out_3 | mask8bit_7_out_3 | mask8bit_8_out_3 | mask8bit_9_out_3 | mask8bit_10_out_3 | mask8bit_11_out_3 | mask8bit_12_out_3;  // OR_Gate or_1, 8 bits wide
endmodule

module Mask8bit (
  input  [7:0] in_1,
  input  in_2,
  output [7:0] out_3
);

  assign out_3 = in_1 & {8{in_2}};  // AND_Gate and_1, 8 bits wide
endmodule

module DMX12x8 (
  input  [7:0] in_1,
  input  [3:0] in_2,
  output [7:0] out_3,
  output [7:0] out_4,
  output [7:0] out_5,
  output [7:0] out_6,
  output [7:0] out_7,
  output [7:0] out_8,
  output [7:0] out_9,
  output [7:0] out_10,
  output [7:0] out_11,
  output [7:0] out_12,
  output [7:0] out_13,
  output [7:0] out_14
);

  wire mux12helper_1_o0, mux12helper_1_o1, mux12helper_1_o2, mux12helper_1_o3, mux12helper_1_o4,
       mux12helper_1_o5, mux12helper_1_o6, mux12helper_1_o7, mux12helper_1_o8, mux12helper_1_o9,
       mux12helper_1_o10, mux12helper_1_o11;

  Mask8bit mask8bit_1 (.in_1(in_1), .in_2(mux12helper_1_o0), .out_3(out_3));
  mux12helper mux12helper_1 (
    .in_1(in_2), .o0(mux12helper_1_o0), .o1(mux12helper_1_o1), .o2(mux12helper_1_o2), .o3(mux12helper_1_o3),
    .o4(mux12helper_1_o4), .o5(mux12helper_1_o5), .o6(mux12helper_1_o6), .o7(mux12helper_1_o7),
    .o8(mux12helper_1_o8), .o9(mux12helper_1_o9), .o10(mux12helper_1_o10), .o11(mux12helper_1_o11));
  Mask8bit mask8bit_2 (.in_1(in_1), .in_2(mux12helper_1_o1), .out_3(out_4));
  Mask8bit mask8bit_3 (.in_1(in_1), .in_2(mux12helper_1_o2), .out_3(out_5));
  Mask8bit mask8bit_4 (.in_1(in_1), .in_2(mux12helper_1_o3), .out_3(out_6));
  Mask8bit mask8bit_5 (.in_1(in_1), .in_2(mux12helper_1_o4), .out_3(out_7));
  Mask8bit mask8bit_6 (.in_1(in_1), .in_2(mux12helper_1_o5), .out_3(out_8));
  Mask8bit mask8bit_7 (.in_1(in_1), .in_2(mux12helper_1_o6), .out_3(out_9));
  Mask8bit mask8bit_8 (.in_1(in_1), .in_2(mux12helper_1_o7), .out_3(out_10));
  Mask8bit mask8bit_9 (.in_1(in_1), .in_2(mux12helper_1_o8), .out_3(out_11));
  Mask8bit mask8bit_10 (.in_1(in_1), .in_2(mux12helper_1_o9), .out_3(out_12));
  Mask8bit mask8bit_11 (.in_1(in_1), .in_2(mux12helper_1_o10), .out_3(out_13));
  Mask8bit mask8bit_12 (.in_1(in_1), .in_2(mux12helper_1_o11), .out_3(out_14));
endmodule

module Mask12x8 (
  input  [7:0] in_1,
  input  [7:0] in_2,
  input  [7:0] in_3,
  input  [7:0] in_4,
  input  [7:0] in_5,
  input  [7:0] in_6,
  input  [7:0] in_7,
  input  [7:0] in_8,
  input  [7:0] in_9,
  input  [7:0] in_10,
  input  [7:0] in_11,
  input  [7:0] in_12,
  input  [11:0] in_13,
  output [7:0] out_14,
  output [7:0] out_15,
  output [7:0] out_16,
  output [7:0] out_17,
  output [7:0] out_18,
  output [7:0] out_19,
  output [7:0] out_20,
  output [7:0] out_21,
  output [7:0] out_22,
  output [7:0] out_23,
  output [7:0] out_24,
  output [7:0] out_25
);

  Mask8bit mask8bit_1 (.in_1(in_1), .in_2(in_13[0]), .out_3(out_14));
  Mask8bit mask8bit_2 (.in_1(in_2), .in_2(in_13[1]), .out_3(out_15));
  Mask8bit mask8bit_3 (.in_1(in_3), .in_2(in_13[2]), .out_3(out_16));
  Mask8bit mask8bit_4 (.in_1(in_4), .in_2(in_13[3]), .out_3(out_17));
  Mask8bit mask8bit_5 (.in_1(in_5), .in_2(in_13[4]), .out_3(out_18));
  Mask8bit mask8bit_6 (.in_1(in_6), .in_2(in_13[5]), .out_3(out_19));
  Mask8bit mask8bit_7 (.in_1(in_7), .in_2(in_13[6]), .out_3(out_20));
  Mask8bit mask8bit_8 (.in_1(in_8), .in_2(in_13[7]), .out_3(out_21));
  Mask8bit mask8bit_9 (.in_1(in_9), .in_2(in_13[8]), .out_3(out_22));
  Mask8bit mask8bit_10 (.in_1(in_10), .in_2(in_13[9]), .out_3(out_23));
  Mask8bit mask8bit_11 (.in_1(in_11), .in_2(in_13[10]), .out_3(out_24));
  Mask8bit mask8bit_12 (.in_1(in_12), .in_2(in_13[11]), .out_3(out_25));
endmodule

module OR12 (
  input  [7:0] in_1,
  input  [7:0] in_2,
  input  [7:0] in_3,
  input  [7:0] in_4,
  input  [7:0] in_5,
  input  [7:0] in_6,
  input  [7:0] in_7,
  input  [7:0] in_8,
  input  [7:0] in_9,
  input  [7:0] in_10,
  input  [7:0] in_11,
  input  [7:0] in_12,
  input  [7:0] in_13,
  input  [7:0] in_14,
  input  [7:0] in_15,
  input  [7:0] in_16,
  input  [7:0] in_17,
  input  [7:0] in_18,
  input  [7:0] in_19,
  input  [7:0] in_20,
  input  [7:0] in_21,
  input  [7:0] in_22,
  input  [7:0] in_23,
  input  [7:0] in_24,
  output [7:0] out_25,
  output [7:0] out_26,
  output [7:0] out_27,
  output [7:0] out_28,
  output [7:0] out_29,
  output [7:0] out_30,
  output [7:0] out_31,
  output [7:0] out_32,
  output [7:0] out_33,
  output [7:0] out_34,
  output [7:0] out_35,
  output [7:0] out_36
);

  assign out_25 = in_1 | in_13;  // OR_Gate or_1, 8 bits wide
  assign out_26 = in_2 | in_14;  // OR_Gate or_2, 8 bits wide
  assign out_27 = in_3 | in_15;  // OR_Gate or_3, 8 bits wide
  assign out_28 = in_4 | in_16;  // OR_Gate or_4, 8 bits wide
  assign out_29 = in_5 | in_17;  // OR_Gate or_5, 8 bits wide
  assign out_30 = in_6 | in_18;  // OR_Gate or_6, 8 bits wide
  assign out_31 = in_7 | in_19;  // OR_Gate or_7, 8 bits wide
  assign out_32 = in_8 | in_20;  // OR_Gate or_8, 8 bits wide
  assign out_33 = in_9 | in_21;  // OR_Gate or_9, 8 bits wide
  assign out_34 = in_10 | in_22;  // OR_Gate or_10, 8 bits wide
  assign out_35 = in_11 | in_23;  // OR_Gate or_11, 8 bits wide
  assign out_36 = in_12 | in_24;  // OR_Gate or_12, 8 bits wide
endmodule

module main (
);

  wire [7:0] displaydriver_1_out_8, displaydriver_1_out_9, displaydriver_1_out_10, displaydriver_1_out_11,
       displaydriver_1_out_12, displaydriver_1_out_13, displaydriver_1_out_14, displaydriver_1_out_15,
       displaydriver_1_out_16, displaydriver_1_out_17, displaydriver_1_out_18, displaydriver_1_out_19;

  DisplayDriver displaydriver_1 (
    .out_8(displaydriver_1_out_8), .out_9(displaydriver_1_out_9), .out_10(displaydriver_1_out_10),
    .out_11(displaydriver_1_out_11), .out_12(displaydriver_1_out_12), .out_13(displaydriver_1_out_13),
    .out_14(displaydriver_1_out_14), .out_15(displaydriver_1_out_15), .out_16(displaydriver_1_out_16),
    .out_17(displaydriver_1_out_17), .out_18(displaydriver_1_out_18), .out_19(displaydriver_1_out_19));  // open: in_1, in_2, in_3, line_shift, Clock, in_6, Reset, read_line_data
  DotMatrix #(.inputtype("row"), .matrixcols(8), .matrixrows(12)) dotmatrix_1 (
    .row0(displaydriver_1_out_8), .row1(displaydriver_1_out_9), .row2(displaydriver_1_out_10),
    .row3(displaydriver_1_out_11), .row4(displaydriver_1_out_12), .row5(displaydriver_1_out_13),
    .row6(displaydriver_1_out_14), .row7(displaydriver_1_out_15), .row8(displaydriver_1_out_16),
    .row9(displaydriver_1_out_17), .row10(displaydriver_1_out_18), .row11(displaydriver_1_out_19));
endmodule
